# Fritzing sketch Buttons+Battery (saved by Fritzing 0.9.2b)
breadboards: 1

parts:
  R2 = Rotary Potentiometer (Large) [maximum_resistance=100kΩ package=THT]
  R3 = Resistor [tolerance=±5% resistance=220 package=THT]
  LED1 = LED - 5mm [color="White (6500K)" package="5 mm [THT]"]
  LED2 = LED - 3mm [color="White (6500K)" package="3 mm [THT]"]
  LED3 = LED - 3mm [color="White (6500K)" package="3 mm [THT]"]
  LED4 = LED - 3mm [color="White (6500K)" package="3 mm [THT]"]
  LED5 = LED - 3mm [color="White (6500K)" package="3 mm [THT]"]
  S1 = Pushbutton [package="[THT]"]
  S2 = Pushbutton [package="[THT]"]
  S3 = Pushbutton [package="[THT]"]
  S4 = Pushbutton [package="[THT]"]
  R4 = Resistor [tolerance=±5% resistance=220 package=THT]
  R5 = Resistor [tolerance=±5% resistance=220 package=THT]
  R6 = Resistor [tolerance=±5% resistance=220 package=THT]
  R7 = Resistor [tolerance=±5% resistance=220 package=THT]
  BAT1 = BC9VPC [package=bc9vpc]

nets:
  N1: R2.leg1, S1.Pin_3, S1.Pin_4, S2.Pin_3, S2.Pin_4, S3.Pin_3, S3.Pin_4, S4.Pin_3, S4.Pin_4, BAT1.V+
  N2: R2.wiper, R3.Pin_0
  N3: R2.leg2, LED1.cathode, LED2.cathode, LED3.cathode, LED4.cathode, LED5.cathode, BAT1.V-
  N4: R3.Pin_1, LED1.anode
  N5: LED2.anode, R7.Pin_1
  N6: LED3.anode, R6.Pin_1
  N7: LED4.anode, R5.Pin_1
  N8: LED5.anode, R4.Pin_1
  N9: S1.Pin_1, S1.Pin_2, R4.Pin_0
  N10: S2.Pin_1, S2.Pin_2, R5.Pin_0
  N11: S3.Pin_1, S3.Pin_2, R6.Pin_0
  N12: S4.Pin_1, S4.Pin_2, R7.Pin_0

notes:
  Backlight LED
  Potmeter can be clicked into breadboard (see photo)
  Side LEDs
